// Digital circuit Template.dig as structural Verilog
module Template (
  input  X0,
  input  X1,
  input  Selector,
  output Z,
  output Z_2
);

  wire and_1_out, and_2_out, not_1_out, or_1_out, or_2_out;

  not not_1 (not_1_out, Selector);
  and and_1 (and_1_out, not_1_out, X0);
  and and_2 (and_2_out, Selector, X1);
  or or_1 (or_1_out, Selector, X0);
  or or_2 (or_2_out, not_1_out, X1);
  and and_3 (Z_2, or_1_out, or_2_out);
  or or_3 (Z, and_1_out, and_2_out);
endmodule
