// Digital circuit Template.dig as structural Verilog
module Template (
  input  X0,
  input  X1,
  input  S1,
  input  X2,
  input  X3,
  input  S0,
  output Z
);

  wire and_1_out, and_2_out, and_3_out, and_4_out, not_1_out, not_2_out;

  not not_1 (not_1_out, S0);
  not not_2 (not_2_out, S1);
  and and_1 (and_1_out, S0, X3, S1);
  and and_2 (and_2_out, S0, X1, not_2_out);
  and and_3 (and_3_out, not_1_out, X2, S1);
  and and_4 (and_4_out, not_2_out, X0, not_1_out);
  or or_1 (Z, and_1_out, and_2_out, and_3_out, and_4_out);
endmodule
