// Digital circuit Template.dig as structural Verilog
module Template (
  input  [2:0] In,
  input  clk,
  output [7:0] Z
);

  wire and_2_out, and_3_out, and_4_out, and_5_out, and_7_out, and_8_out, and_9_out, and_10_out, and_11_out,
       and_12_out, and_13_out, and_14_out, and_15_out, and_16_out, and_17_out, not_1_out, not_2_out,
       not_3_out;

  not not_1 (not_1_out, In[2]);
  not not_2 (not_2_out, In[1]);
  not not_3 (not_3_out, In[0]);
  and and_1 (Z[7], not_3_out, In[0]);
  or or_1 (Z[6], In[0], not_3_out);
  and and_2 (and_2_out, not_1_out, not_2_out, In[0]);
  and and_3 (and_3_out, In[2], not_3_out);
  and and_4 (and_4_out, In[1], not_3_out);
  and and_5 (and_5_out, In[2], In[1]);
  and and_6 (Z[4], In[0], not_3_out);
  and and_7 (and_7_out, In[2], not_2_out);
  and and_8 (and_8_out, not_1_out, In[0]);
  and and_9 (and_9_out, not_3_out, not_2_out);
  and and_10 (and_10_out, In[2], not_2_out);
  and and_11 (and_11_out, not_1_out, In[1]);
  and and_12 (and_12_out, In[2], not_2_out, not_3_out);
  and and_13 (and_13_out, not_1_out, In[1], not_3_out);
  and and_14 (and_14_out, In[2], In[1], In[0]);
  and and_15 (and_15_out, In[0], not_2_out, not_1_out);
  and and_16 (and_16_out, In[2], not_3_out);
  and and_17 (and_17_out, In[1], not_3_out);
  or or_2 (Z[5], and_2_out, and_3_out, and_4_out, and_5_out);
  or or_3 (Z[3], and_7_out, and_8_out);
  or or_4 (Z[2], and_9_out, and_10_out, and_11_out);
  or or_5 (Z[1], and_12_out, and_13_out, and_14_out);
  or or_6 (Z[0], and_15_out, and_16_out, and_17_out);
  Terminal terminal_1 (.D(Z), .C(clk), .en(1'b1));
endmodule
