// Digital circuit 2421.dig as structural Verilog
module _2421 (
  input  [3:0] inp,
  output [3:0] op
);

  wire and_1_out, and_2_out, and_3_out, and_4_out, and_5_out, and_6_out, not_1_out, not_2_out, not_3_out;

  not not_1 (not_1_out, inp[2]);
  not not_2 (not_2_out, inp[1]);
  not not_3 (not_3_out, inp[0]);
  and and_1 (and_1_out, inp[2], not_2_out, inp[0]);
  and and_2 (and_2_out, inp[2], inp[1]);
  and and_3 (and_3_out, inp[2], not_3_out);
  and and_4 (and_4_out, inp[2], inp[1]);
  and and_5 (and_5_out, not_1_out, inp[1]);
  and and_6 (and_6_out, inp[2], not_2_out, inp[0]);
  or or_1 (op[3], inp[3], and_1_out, and_2_out);
  or or_2 (op[2], inp[3], and_3_out, and_4_out);
  or or_3 (op[1], inp[3], and_5_out, and_6_out);

  assign op[0] = inp[0];
endmodule
