// Digital circuit ROM.dig as structural Verilog
module ROM (
  input  [3:0] In,
  input  [1:0] selector,
  output [3:0] \output 
);

  wire [3:0] _2421_d, _6423_d, Cyclic_d, Ex3_d;

  ROM #(.AddrBits(4), .Bits(4)) Ex3 (.A(In), .sel(1'b1), .D(Ex3_d));
  ROM #(.AddrBits(4), .Bits(4)) Cyclic (.A(In), .sel(1'b1), .D(Cyclic_d));
  ROM #(.AddrBits(4), .Bits(4)) _2421 (.A(In), .sel(1'b1), .D(_2421_d));
  ROM #(.AddrBits(4), .Bits(4)) _6423 (.A(In), .sel(1'b1), .D(_6423_d));
  Multiplexer #(.Bits(4), .Selector_Bits(2)) multiplexer_1 (
    .sel(selector), .in_0(Ex3_d), .in_1(Cyclic_d), .in_2(_2421_d), .in_3(_6423_d), .out(\output ));

  // Notes on the sheet:
  //   contents of Ex3 (hex, n*v repeats v):
  //   3,4,5,6,7,8,9,a,b,c
  //   contents of Cyclic (hex, n*v repeats v):
  //   0,1,3,2,6,7,6,4,c,d
  //   contents of _2421 (hex, n*v repeats v):
  //   0,1,2,3,4,b,c,d,e,f
  //   contents of _6423 (hex, n*v repeats v):
  //   0,5,2,9,4,b,6,d,a,f
endmodule
