// Digital circuit Templatet.dig as structural Verilog
module Templatet (
  input  [3:0] In,
  input  [1:0] Selector,
  output [3:0] Output
);

  wire [3:0] _2421_1_op, _6423_1_op, cyclic_1_output, excess3_1_op;

  excess3 excess3_1 (.inp(In), .op(excess3_1_op));
  cyclic cyclic_1 (.\input (In), .\output (cyclic_1_output));
  _2421 _2421_1 (.inp(In), .op(_2421_1_op));
  _6423 _6423_1 (.inp(In), .op(_6423_1_op));
  selector selector_1 (
    .X0(excess3_1_op), .X1(cyclic_1_output), .X2(_2421_1_op), .X3(_6423_1_op), .S0(Selector), .op(Output));
endmodule
