// Digital circuit cyclic.dig as structural Verilog
module cyclic (
  input  [3:0] \input ,
  output [3:0] \output 
);

  xor xor_1 (\output [0], \input [0], \input [1]);
  xor xor_2 (\output [1], \input [1], \input [2]);
  xor xor_3 (\output [2], \input [2], \input [3]);

  assign \output [3] = \input [3];
endmodule
