// Digital circuit excess3.dig as structural Verilog
module excess3 (
  input  [3:0] inp,
  output [3:0] op
);

  wire and_1_out, and_2_out, and_3_out, and_4_out, and_5_out, and_6_out, and_7_out, and_8_out, and_9_out,
       and_10_out, not_1_out, not_2_out, not_3_out;

  not not_1 (not_1_out, inp[2]);
  not not_2 (not_2_out, inp[1]);
  not not_3 (not_3_out, inp[0]);
  and and_1 (and_1_out, inp[2], inp[1], not_3_out);
  and and_2 (and_2_out, inp[2], inp[0]);
  and and_3 (and_3_out, inp[2], not_2_out, not_3_out);
  and and_4 (and_4_out, not_1_out, inp[1], not_3_out);
  and and_5 (and_5_out, not_1_out, inp[0]);
  and and_6 (and_6_out, inp[1], inp[0]);
  and and_7 (and_7_out, not_2_out, not_3_out);
  and and_8 (and_8_out, not_1_out, inp[1], not_3_out);
  and and_9 (and_9_out, inp[2], inp[1], not_3_out);
  and and_10 (and_10_out, not_2_out, not_3_out);
  or or_1 (op[3], inp[3], and_1_out, and_2_out);
  or or_2 (op[2], and_3_out, and_4_out, and_5_out);
  or or_3 (op[1], and_6_out, and_7_out);
  or or_4 (op[0], and_8_out, and_9_out, and_10_out);
endmodule
