// Digital circuit selector.dig as structural Verilog
module selector (
  input  [3:0] X0,
  input  [3:0] X1,
  input  [3:0] X2,
  input  [3:0] X3,
  input  [1:0] S0,
  output [3:0] op
);

  wire not_1_out, not_2_out;
  wire [3:0] and_5_out, and_6_out, and_7_out, and_8_out;
  wire [3:3] and_1_out, and_2_out, and_3_out, and_4_out;

  not not_1 (not_1_out, S0[0]);
  not not_2 (not_2_out, S0[1]);
  and and_1 (and_1_out[3], not_2_out, not_1_out);
  and and_2 (and_2_out[3], S0[0], not_2_out);
  and and_3 (and_3_out[3], S0[1], not_1_out);
  and and_4 (and_4_out[3], S0[0], S0[1]);
  assign and_5_out = {4{and_1_out[3]}} & X0;  // And and_5, 4 bits wide
  assign and_6_out = {4{and_2_out[3]}} & X1;  // And and_6, 4 bits wide
  assign and_7_out = {4{and_3_out[3]}} & X2;  // And and_7, 4 bits wide
  assign and_8_out = {4{and_4_out[3]}} & X3;  // And and_8, 4 bits wide
  assign op = and_5_out | and_6_out | and_7_out | and_8_out;  // Or or_1, 4 bits wide
endmodule
