// Digital circuit ErrorDetector.dig as structural Verilog
module ErrorDetector (
  input  [6:0] i,
  output c1,
  output c2,
  output c3
);

  xor xor_1 (c1, i[0], i[1], i[2], i[3]);
  xor xor_2 (c2, i[0], i[1], i[4], i[5]);
  xor xor_3 (c3, i[6], i[4], i[2], i[0]);
endmodule
