// Digital circuit Template.dig as structural Verilog
module Template (
  input  [6:0] In,
  output [6:0] Output
);

  wire errordetector_1_c1, errordetector_1_c2, errordetector_1_c3;
  wire [6:0] inverter_1_o;

  ErrorDetector errordetector_1 (.i(In), .c1(errordetector_1_c1), .c2(errordetector_1_c2), .c3(errordetector_1_c3));
  inverter inverter_1 (.c1(errordetector_1_c1), .c2(errordetector_1_c2), .c3(errordetector_1_c3), .o(inverter_1_o));
  assign Output = inverter_1_o ^ In;  // XOr xor_1, 7 bits wide
endmodule
