// Digital circuit inverter.dig as structural Verilog
module inverter (
  input  c1,
  input  c2,
  input  c3,
  output [6:0] o
);

  wire not_1_out, not_2_out, not_3_out;

  not not_1 (not_1_out, c1);
  not not_2 (not_2_out, c2);
  not not_3 (not_3_out, c3);
  and and_1 (o[6], not_1_out, not_2_out, c3);
  and and_2 (o[5], not_1_out, c2, not_3_out);
  and and_3 (o[4], not_1_out, c2, c3);
  and and_4 (o[3], c1, not_2_out, not_3_out);
  and and_5 (o[2], c1, not_2_out, c3);
  and and_6 (o[1], c1, c2, not_3_out);
  and and_7 (o[0], c1, c2, c3);
endmodule
