// Digital circuit Template.dig as structural Verilog
module Template (
  input  A,
  input  B,
  input  C,
  input  D,
  output Before,
  output After
);

  wire and_1_out, and_2_out, nand_1_out, nand_2_out;

  and and_1 (and_1_out, ~C, D);  // And
  and and_2 (and_2_out, A, ~B, D);  // And
  nand nand_1 (nand_1_out, ~C, D);  // NAnd
  nand nand_2 (nand_2_out, ~B, D);  // NAnd
  or or_1 (Before, and_1_out, ~A, and_2_out);  // Or
  nand nand_3 (After, A, nand_1_out, nand_2_out);
endmodule

/* Test case T1:
A B C D Before After
0 0 1 1 1 1
1 0 1 1 1 1
1 0 1 1 1 1
*/
