// Digital circuit Template.dig as structural Verilog
module Template (
  input  A,
  input  B,
  input  C,
  input  D,
  input  E,
  input  F,
  output Before,
  output After
);

  wire and_1_out, and_2_out, and_3_out, and_4_out, and_5_out, and_6_out, and_7_out, and_8_out;

  and and_1 (and_1_out, ~A, ~B, E, F);  // And
  and and_2 (and_2_out, ~A, ~C, ~D, ~E);  // And
  and and_3 (and_3_out, ~A, D, ~E, ~F);  // And
  and and_4 (and_4_out, ~A, ~B, E, F);  // And
  and and_5 (and_5_out, ~A, ~C, ~D, ~E);  // And
  and and_6 (and_6_out, ~A, D, ~E, ~F);  // And
  and and_7 (and_7_out, ~A, ~C, ~E, ~F);  // And
  and and_8 (and_8_out, ~A, ~B, ~C, ~D, F);  // And
  or or_1 (Before, and_1_out, and_2_out, and_3_out);
  or or_2 (After, and_4_out, and_5_out, and_6_out, and_7_out, and_8_out);
endmodule

/* Test case test1:
A B C D E F Before After
0 0 0 0 0 0 1 1
0 0 0 0 0 1 1 1
0 0 0 0 1 0 0 0
0 0 0 0 1 1 1 1
0 0 0 1 0 0 1 1
0 0 0 1 0 1 0 0
0 0 0 1 1 0 0 0
0 0 0 1 1 1 1 1
0 0 1 0 0 0 0 0
0 0 1 0 0 1 0 0
0 0 1 0 1 0 0 0
0 0 1 0 1 1 1 1
0 0 1 1 0 0 1 1
0 0 1 1 0 1 0 0
0 0 1 1 1 0 0 0
0 0 1 1 1 1 1 1
0 1 0 0 0 0 1 1
0 1 0 0 0 1 1 1
0 1 0 0 1 0 0 0
0 1 0 0 1 1 0 0
0 1 0 1 0 0 1 1
0 1 0 1 0 1 0 0
0 1 0 1 1 0 0 0
0 1 0 1 1 1 0 0
0 1 1 0 0 0 0 0
0 1 1 0 0 1 0 0
0 1 1 0 1 0 0 0
0 1 1 0 1 1 0 0
0 1 1 1 0 0 1 1
0 1 1 1 0 1 0 0
0 1 1 1 1 0 0 0
0 1 1 1 1 1 0 0
*/

/* Test case test2:
A B C D E F Before After
0 0 0 1 0 0 1 1
0 0 0 0 0 0 1 1
0 0 0 1 0 0 1 1
0 0 0 0 0 0 1 1
*/

/* Test case test3:
A B C D E F Before After
0 1 0 1 0 0 1 1
0 1 0 0 0 0 1 1
0 1 0 1 0 0 1 1
0 1 0 0 0 0 1 1
*/

/* Test case test4:
A B C D E F Before After
0 0 0 0 1 1 1 1
0 0 0 0 0 1 1 1
0 0 0 0 1 1 1 1
0 0 0 0 0 1 1 1
*/
