// Digital circuit Solution.dig as structural Verilog
module Solution (
  input  [3:0] In,
  output [3:0] Output
);

  wire [3:0] add_1_s, not_1_out;

  assign not_1_out = ~{1'b0, In[2:0]};  // Not not_1, 4 bits wide
  Add #(.Bits(4)) add_1 (.a(not_1_out), .b(4'b0000), .c_i(1'b1), .s(add_1_s));  // open: c_o
  Multiplexer #(.Bits(4)) multiplexer_1 (.sel(In[3]), .in_0(In), .in_1(add_1_s), .out(Output));

  // Other names for the same wires on the sheet: A[2:0] = In[2:0]; S = In[3]
endmodule
