// Digital circuit M1.dig as structural Verilog
module M1 (
  input  [3:0] A,
  input  [3:0] B,
  input  [2:0] S,
  input  C,
  output [3:0] out
);

  wire [3:0] add_1_s, add_2_s, add_3_s, add_4_s, add_5_s, add_6_s, add_7_s, negative_1_a_2, negative_2_a_2,
       not_1_out;

  Add #(.Bits(4)) add_1 (.a(B), .b(4'b0001), .c_i(1'b0), .s(add_1_s));  // open: c_o
  assign not_1_out = ~A;  // Not not_1, 4 bits wide
  negative negative_1 (.A(4'b0001), .A_2(negative_1_a_2));
  negative negative_2 (.A(add_1_s), .A_2(negative_2_a_2));
  Add #(.Bits(4)) add_2 (.a(A), .b(4'b0000), .c_i(C), .s(add_2_s));  // open: c_o
  Add #(.Bits(4)) add_3 (.a(A), .b(negative_1_a_2), .c_i(C), .s(add_3_s));  // open: c_o
  Add #(.Bits(4)) add_4 (.a(A), .b(B), .c_i(C), .s(add_4_s));  // open: c_o
  Add #(.Bits(4)) add_5 (.a(A), .b(negative_2_a_2), .c_i(C), .s(add_5_s));  // open: c_o
  Add #(.Bits(4)) add_6 (.a(not_1_out), .b(4'b0000), .c_i(C), .s(add_6_s));  // open: c_o
  Add #(.Bits(4)) add_7 (.a(B), .b(4'b0000), .c_i(C), .s(add_7_s));  // open: c_o
  Multiplexer #(.Selector_Bits(3), .Bits(4)) multiplexer_1 (
    .sel(S), .in_0(add_2_s), .in_1(add_3_s), .in_2(add_4_s), .in_3(add_5_s), .in_4(add_6_s), .in_5(add_7_s),
    .in_6({A[2:0], 1'b0}), .in_7({1'b0, A[3:1]}), .out(out));
endmodule
