// Digital circuit Template.dig as structural Verilog
module Template (
  input  [3:0] A,
  input  [3:0] B,
  input  [2:0] S,
  input  M,
  input  C,
  output [3:0] F
);

  wire [3:0] m0_1_out, m1_1_out;

  M0 m0_1 (.A(A), .B(B), .S(S), .out(m0_1_out));
  M1 m1_1 (.A(A), .B(B), .S(S), .C(C), .out(m1_1_out));
  Multiplexer #(.Bits(4)) multiplexer_1 (.sel(M), .in_0(m0_1_out), .in_1(m1_1_out), .out(F));

  // Other names for the same wires on the sheet: selector[2:0] = S
endmodule
