// Digital circuit negative.dig as structural Verilog
module negative (
  input  [3:0] A,
  output [3:0] A_2
);

  wire [3:0] not_1_out;

  assign not_1_out = ~A;  // Not not_1, 4 bits wide
  Add #(.Bits(4)) add_1 (.a(not_1_out), .b(4'b0001), .c_i(1'b0), .s(A_2));  // open: c_o
endmodule
