// Digital circuit Template.dig as structural Verilog
module Template (
  input  P,
  input  T,
  input  D,
  input  C,
  input  B,
  input  A,
  input  Clr,
  input  Load,
  input  Clock,
  output QD,
  output QC,
  output QB,
  output QA,
  output RCO
);

  wire and_1_out, and_2_out, not_1_out, not_2_out;
  wire [3:0] add_1_s, multiplexer_1_out, multiplexer_2_out, multiplexer_3_out;

  not not_1 (not_1_out, Clr);
  Multiplexer #(.Bits(4)) multiplexer_1 (
    .sel(and_1_out), .in_0({QD, QC, QB, QA}), .in_1(4'b0000), .out(multiplexer_1_out));
  not not_2 (not_2_out, Load);
  and and_1 (and_1_out, Load, not_1_out);
  and and_2 (and_2_out, P, T, Clr, Load);
  Multiplexer #(.Bits(4)) multiplexer_2 (
    .sel(not_2_out), .in_0(multiplexer_1_out), .in_1({D, C, B, A}), .out(multiplexer_2_out));
  Add #(.Bits(4)) add_1 (.a({QD, QC, QB, QA}), .b(4'b0000), .c_i(1'b1), .s(add_1_s));  // open: c_o
  Multiplexer #(.Bits(4)) multiplexer_3 (
    .sel(and_2_out), .in_0(multiplexer_2_out), .in_1(add_1_s), .out(multiplexer_3_out));
  D_FF #(.Bits(4)) d_ff_1 (.D(multiplexer_3_out), .C(Clock), .Q({QD, QC, QB, QA}));  // open: nQ
  and and_3 (RCO, QD, QC, QB, QA);
endmodule
