// Digital circuit Template.dig as structural Verilog
module Template (
  input  P,
  input  Clr,
  input  clock,
  output Z
);

  wire and_1_out, and_2_out, d_ff_1_nq;

  and and_1 (and_1_out, ~Clr, P);  // And
  D_FF d_ff_1 (.D(and_1_out), .C(clock), .nQ(d_ff_1_nq));  // open: Q
  and and_2 (and_2_out, and_1_out, d_ff_1_nq);
  D_FF d_ff_2 (.D(and_2_out), .C(clock), .Q(Z));  // open: nQ
endmodule
