// Digital circuit Template.dig as structural Verilog
module Template (
  input  P,
  input  Clr,
  input  clock,
  output Z
);

  wire and_1_out, and_2_out, d_ff_1_q, d_ff_2_nq;

  D_FF d_ff_1 (.D(P), .C(clock), .Q(d_ff_1_q));  // open: nQ
  and and_1 (and_1_out, ~Clr, d_ff_1_q);  // And
  D_FF d_ff_2 (.D(and_1_out), .C(clock), .nQ(d_ff_2_nq));  // open: Q
  and and_2 (and_2_out, and_1_out, d_ff_2_nq);
  D_FF d_ff_3 (.D(and_2_out), .C(clock), .Q(Z));  // open: nQ
endmodule
