// Digital circuit Template.dig as structural Verilog
module Template (
  input  A,
  input  B,
  input  Clr,
  input  Clock,
  output Z
);

  wire add_1_c_o, and_1_out, and_2_out, and_3_out, d_ff_1_q;

  and and_1 (and_1_out, Clr, A);
  and and_2 (and_2_out, Clr, B);
  and and_3 (and_3_out, Clr, d_ff_1_q);
  Add add_1 (.a(and_1_out), .b(and_2_out), .c_i(and_3_out), .s(Z), .c_o(add_1_c_o));
  D_FF d_ff_1 (.D(add_1_c_o), .C(Clock), .Q(d_ff_1_q));  // open: nQ
endmodule
