// Digital circuit Template_3.dig as structural Verilog
module Template_3 (
  input  P,
  input  Clr,
  input  clock,
  output Z,
  output trigger
);

  wire and_1_out, and_2_out, and_3_out, and_4_out, and_5_out, or_1_out;

  and and_1 (and_1_out, ~Z, P, ~trigger);  // And
  and and_2 (and_2_out, ~Z, P, trigger);  // And
  and and_3 (and_3_out, Z, P, trigger);
  or or_1 (or_1_out, and_1_out, and_2_out, and_3_out);
  and and_4 (and_4_out, and_1_out, ~Clr);  // And
  and and_5 (and_5_out, or_1_out, ~Clr);  // And
  D_FF d_ff_1 (.D(and_4_out), .C(clock), .Q(Z));  // open: nQ
  D_FF d_ff_2 (.D(and_5_out), .C(clock), .Q(trigger));  // open: nQ
endmodule
