// Digital circuit try.dig as structural Verilog
module try (
  input  Load,
  input  P,
  input  T,
  input  Clr,
  input  D,
  input  C,
  input  B,
  input  A,
  input  Clock,
  output QD,
  output QC,
  output QB,
  output QA,
  output RCO
);

  wire PT;
  wire [3:0] add_1_s, multiplexer_1_out;

  Add #(.Bits(4)) add_1 (.a({QD, QC, QB, QA}), .b(4'b0000), .c_i(1'b1), .s(add_1_s));  // open: c_o
  and and_1 (PT, P, T);
  Multiplexer #(.Bits(4), .Selector_Bits(3)) multiplexer_1 (
    .sel({PT, Load, Clr}), .in_0({D, C, B, A}), .in_1({D, C, B, A}), .in_2(4'b0000), .in_3({QD, QC, QB, QA}),
    .in_4({D, C, B, A}), .in_5({D, C, B, A}), .in_6(4'b0000), .in_7(add_1_s), .out(multiplexer_1_out));
  D_FF #(.Bits(4)) d_ff_1 (.D(multiplexer_1_out), .C(Clock), .Q({QD, QC, QB, QA}));  // open: nQ
  and and_2 (RCO, QD, QC, QB, QA);
endmodule
