// Digital circuit Template.dig as structural Verilog
module Template (
  input  P5,
  input  reset,
  input  clock,
  input  P10,
  input  P20,
  input  Pcoffee,
  input  Ptea,
  input  Pchange,
  input  Pnext,
  output [5:0] Balance,
  output CoffeeOut,
  output TeaOut,
  output [1:0] Change5,
  output [1:0] Change10,
  output [1:0] Change20
);

  wire and_1_out, and_2_out, and_3_out, and_4_out, and_5_out, and_6_out, and_7_out, and_16_out, and_17_out,
       and_18_out, and_19_out, comparator_1_gt, comparator_2_eq, comparator_2_gt, d_ff_1_nq, d_ff_2_nq,
       d_ff_3_nq, d_ff_4_nq, d_ff_5_nq, d_ff_6_nq, d_ff_7_nq, hold, multiplexer_6_out, multiplexer_7_out,
       nor_2_out, not_1_out, not_2_out, not_3_out, or_1_out, or_2_out, or_3_out, or_4_out, or_5_out,
       or_6_out, p5_t, p10_t, p20_t, pc, pchange_t, pnext_t, pt;
  wire [5:0] add_1_s, add_2_s, add_3_s, and_8_out, and_9_out, and_10_out, and_11_out, and_12_out, and_13_out,
       and_15_out, bitextender_1_out, bitextender_2_out, bitextender_3_out, bitextender_4_out,
       bitextender_5_out, bitextender_6_out, bitextender_7_out, bitextender_8_out, bitextender_9_out,
       bitextender_10_out, div_1_q, div_1_r, div_2_q, div_2_r, div_3_q, multiplexer_1_out, multiplexer_2_out,
       multiplexer_3_out, multiplexer_4_out, multiplexer_5_out, sub_1_s, subv;
  wire [5:2] C5, C10, C20;

  D_FF d_ff_1 (.D(Pcoffee), .C(clock), .nQ(d_ff_1_nq));  // open: Q
  D_FF d_ff_2 (.D(Ptea), .C(clock), .nQ(d_ff_2_nq));  // open: Q
  D_FF d_ff_3 (.D(Pchange), .C(clock), .nQ(d_ff_3_nq));  // open: Q
  D_FF d_ff_4 (.D(Pnext), .C(clock), .nQ(d_ff_4_nq));  // open: Q
  D_FF d_ff_5 (.D(P5), .C(clock), .nQ(d_ff_5_nq));  // open: Q
  D_FF d_ff_6 (.D(P10), .C(clock), .nQ(d_ff_6_nq));  // open: Q
  D_FF d_ff_7 (.D(P20), .C(clock), .nQ(d_ff_7_nq));  // open: Q
  and and_1 (and_1_out, Ptea, d_ff_2_nq);
  and and_2 (and_2_out, Pchange, d_ff_3_nq);
  and and_3 (and_3_out, P5, d_ff_5_nq);
  and and_4 (and_4_out, P10, d_ff_6_nq);
  and and_5 (and_5_out, P20, d_ff_7_nq);
  and and_6 (and_6_out, Pcoffee, d_ff_1_nq);
  D_FF d_ff_8 (.D(and_1_out), .C(clock), .Q(pt));  // open: nQ
  D_FF d_ff_9 (.D(and_2_out), .C(clock), .Q(pchange_t));  // open: nQ
  and and_7 (and_7_out, Pnext, d_ff_4_nq);
  BitExtender #(.inputBits(1), .outputBits(6)) bitextender_1 (.in(hold), .out(bitextender_1_out));
  D_FF d_ff_10 (.D(and_3_out), .C(clock), .Q(p5_t));  // open: nQ
  D_FF d_ff_11 (.D(and_4_out), .C(clock), .Q(p10_t));  // open: nQ
  D_FF d_ff_12 (.D(and_5_out), .C(clock), .Q(p20_t));  // open: nQ
  D_FF d_ff_13 (.D(and_6_out), .C(clock), .Q(pc));  // open: nQ
  D_FF d_ff_14 (.D(and_7_out), .C(clock), .Q(pnext_t));  // open: nQ
  BitExtender #(.inputBits(1), .outputBits(6)) bitextender_2 (.in(p5_t), .out(bitextender_2_out));
  BitExtender #(.inputBits(1), .outputBits(6)) bitextender_3 (.in(p10_t), .out(bitextender_3_out));
  BitExtender #(.inputBits(1), .outputBits(6)) bitextender_4 (.in(p20_t), .out(bitextender_4_out));
  assign and_8_out = bitextender_2_out & bitextender_1_out & 6'b000101;  // And and_8, 6 bits wide
  assign and_9_out = bitextender_3_out & bitextender_1_out & 6'b001010;  // And and_9, 6 bits wide
  assign and_10_out = bitextender_4_out & bitextender_1_out & 6'b010100;  // And and_10, 6 bits wide
  or or_1 (or_1_out, pchange_t, reset);
  Add #(.Bits(6)) add_1 (.a(and_8_out), .b(and_9_out), .c_i(1'b0), .s(add_1_s));  // open: c_o
  not not_1 (not_1_out, reset);
  Add #(.Bits(6)) add_2 (.a(add_1_s), .b(and_10_out), .c_i(1'b0), .s(add_2_s));  // open: c_o
  BitExtender #(.inputBits(1), .outputBits(6)) bitextender_5 (.in(pchange_t), .out(bitextender_5_out));
  BitExtender #(.inputBits(1), .outputBits(6)) bitextender_6 (.in(not_1_out), .out(bitextender_6_out));
  Add #(.Bits(6)) add_3 (.a(add_2_s), .b(Balance), .c_i(1'b0), .s(add_3_s));  // open: c_o
  Div #(.Bits(6)) div_1 (.a(Balance), .b(6'b010100), .q(div_1_q), .r(div_1_r));
  nor nor_1 (hold, CoffeeOut, TeaOut);
  Multiplexer #(.Bits(6)) multiplexer_1 (
    .sel(or_1_out), .in_0({C20, Change20}), .in_1(and_11_out), .out(multiplexer_1_out));
  assign and_11_out = bitextender_5_out & bitextender_6_out & div_1_q;  // And and_11, 6 bits wide
  or or_2 (or_2_out, pc, pt);
  D_FF #(.Bits(6)) d_ff_15 (.D(multiplexer_1_out), .C(clock), .Q({C20, Change20}));  // open: nQ
  Div #(.Bits(6)) div_2 (.a(div_1_r), .b(6'b001010), .q(div_2_q), .r(div_2_r));
  // Probe on {C20, Change20}
  Multiplexer #(.Bits(6)) multiplexer_2 (
    .sel(or_1_out), .in_0({C10, Change10}), .in_1(and_12_out), .out(multiplexer_2_out));
  assign and_12_out = bitextender_5_out & bitextender_6_out & div_2_q;  // And and_12, 6 bits wide
  BitExtender #(.inputBits(1), .outputBits(6)) bitextender_7 (.in(or_3_out), .out(bitextender_7_out));
  Comparator #(.Bits(6)) comparator_1 (.a(add_3_s), .b(6'b110010), .gt(comparator_1_gt));  // open: eq, lt
  D_FF #(.Bits(6)) d_ff_16 (.D(multiplexer_2_out), .C(clock), .Q({C10, Change10}));  // open: nQ
  Div #(.Bits(6)) div_3 (.a(div_2_r), .b(6'b000101), .q(div_3_q));  // open: r
  Multiplexer #(.Bits(6)) multiplexer_3 (.sel(pc), .in_0(6'b010100), .in_1(6'b011001), .out(multiplexer_3_out));
  BitExtender #(.inputBits(1), .outputBits(6)) bitextender_8 (.in(or_2_out), .out(bitextender_8_out));
  BitExtender #(.inputBits(1), .outputBits(6)) bitextender_9 (.in(hold), .out(bitextender_9_out));
  // Probe on {C10, Change10}
  Multiplexer #(.Bits(6)) multiplexer_4 (
    .sel(or_1_out), .in_0({C5, Change5}), .in_1(and_13_out), .out(multiplexer_4_out));
  assign and_13_out = bitextender_5_out & bitextender_6_out & div_3_q;  // And and_13, 6 bits wide
  assign subv = multiplexer_3_out & bitextender_7_out & bitextender_8_out & bitextender_9_out;  // And and_14, 6 bits wide
  Multiplexer #(.Bits(6)) multiplexer_5 (
    .sel(comparator_1_gt), .in_0(add_3_s), .in_1(Balance), .out(multiplexer_5_out));
  nor nor_2 (nor_2_out, reset, pchange_t);
  D_FF #(.Bits(6)) d_ff_17 (.D(multiplexer_4_out), .C(clock), .Q({C5, Change5}));  // open: nQ
  Comparator #(.Bits(6)) comparator_2 (
    .a(Balance), .b(multiplexer_3_out), .gt(comparator_2_gt), .eq(comparator_2_eq));  // open: lt
  Sub #(.Bits(6)) sub_1 (.a(multiplexer_5_out), .b(subv), .c_i(1'b0), .s(sub_1_s));  // open: c_o
  // Probe on {C5, Change5}
  or or_3 (or_3_out, comparator_2_gt, comparator_2_eq);
  BitExtender #(.inputBits(1), .outputBits(6)) bitextender_10 (.in(nor_2_out), .out(bitextender_10_out));
  assign and_15_out = sub_1_s & bitextender_10_out;  // And and_15, 6 bits wide
  D_FF #(.Bits(6)) Bal (.D(and_15_out), .C(clock), .Q(Balance));  // open: nQ
  and and_16 (and_16_out, or_3_out, hold, pc);
  and and_17 (and_17_out, or_3_out, hold, pt);
  or or_4 (or_4_out, pnext_t, reset, pchange_t);
  // Probe on Balance
  or or_5 (or_5_out, and_16_out, or_4_out);
  or or_6 (or_6_out, and_17_out, or_4_out);
  not not_2 (not_2_out, or_4_out);
  not not_3 (not_3_out, or_4_out);
  and and_18 (and_18_out, not_2_out, and_16_out);
  and and_19 (and_19_out, not_3_out, and_17_out);
  Multiplexer multiplexer_6 (.sel(or_5_out), .in_0(CoffeeOut), .in_1(and_18_out), .out(multiplexer_6_out));
  Multiplexer multiplexer_7 (.sel(or_6_out), .in_0(TeaOut), .in_1(and_19_out), .out(multiplexer_7_out));
  D_FF d_ff_18 (.D(multiplexer_7_out), .C(clock), .Q(TeaOut));  // open: nQ
  D_FF d_ff_19 (.D(multiplexer_6_out), .C(clock), .Q(CoffeeOut));  // open: nQ

  // Other names for the same wires on the sheet: bal[5:0] = Balance; C5[1:0] = Change5; C10[1:0] = Change10;
  //   C20[1:0] = Change20; CO = CoffeeOut; TO = TeaOut
endmodule
