// Digital circuit 2559_1.dig as structural Verilog
module _2559_1 (
  input  warning,
  input  clk,
  input  car,
  input  human
);

  wire and_1_out, and_2_out, and_3_out, and_4_out, and_5_out, and_6_out, carcase, comparator_1_eq,
       comparator_1_lt, comparator_2_eq, comparator_2_lt, comparator_3_eq, counter_1_out, counter_2_out,
       d_ff_1_nq, humcase, instantflip, jk_ff_1_q, jk_ff_2_q, not_1_out, or_1_out, or_3_out, statechange,
       warncase;
  wire [1:0] multiplexer_4_out, multiplexer_6_out, multiplexer_7_out, state_q;
  wire [1:1] warnAns;
  wire [2:0] and_7_out, and_8_out, bitextender_1_out, bitextender_2_out, multiplexer_1_out,
       multiplexer_2_out, multiplexer_3_out, multiplexer_5_out, multiplexer_8_out, multiplexer_9_out,
       or_2_out, warnToOtherAns;

  and and_1 (and_1_out, carcase, human);
  and and_2 (and_2_out, humcase, car);
  JK_FF jk_ff_1 (.J(and_1_out), .C(clk), .K(statechange), .Q(jk_ff_1_q));  // open: nQ
  JK_FF jk_ff_2 (.J(and_2_out), .C(clk), .K(statechange), .Q(jk_ff_2_q));  // open: nQ
  and and_3 (and_3_out, jk_ff_1_q, comparator_1_lt);
  and and_4 (and_4_out, jk_ff_2_q, comparator_2_lt);
  and and_5 (and_5_out, car, warncase);
  and and_6 (and_6_out, warncase, human);
  Counter counter_1 (.en(and_3_out), .C(clk), .clr(statechange), .out(counter_1_out));  // open: ovf
  Counter counter_2 (.en(and_4_out), .C(clk), .clr(statechange), .out(counter_2_out));  // open: ovf
  or or_1 (or_1_out, and_6_out, and_5_out);
  BitExtender #(.inputBits(1), .outputBits(3)) bitextender_1 (.in(and_5_out), .out(bitextender_1_out));
  BitExtender #(.inputBits(1), .outputBits(3)) bitextender_2 (.in(and_6_out), .out(bitextender_2_out));
  assign and_7_out = bitextender_1_out & 3'b001;  // And and_7, 3 bits wide
  assign and_8_out = bitextender_2_out & 3'b100;  // And and_8, 3 bits wide
  JK_FF jk_ff_3 (.J(or_1_out), .C(clk), .K(statechange), .Q(instantflip));  // open: nQ
  Comparator comparator_1 (.a(counter_1_out), .b(1'b1), .eq(comparator_1_eq), .lt(comparator_1_lt));  // open: gt
  Comparator comparator_2 (.a(counter_2_out), .b(1'b1), .eq(comparator_2_eq), .lt(comparator_2_lt));  // open: gt
  assign or_2_out = and_7_out | and_8_out;  // Or or_2, 3 bits wide
  Multiplexer #(.Bits(3)) multiplexer_1 (
    .sel(or_1_out), .in_0(warnToOtherAns), .in_1(or_2_out), .out(multiplexer_1_out));
  Multiplexer #(.Bits(3)) multiplexer_2 (.sel(comparator_1_eq), .in_0(3'b010), .in_1(3'b100), .out(multiplexer_2_out));
  Multiplexer #(.Bits(3)) multiplexer_3 (.sel(comparator_2_eq), .in_0(3'b010), .in_1(3'b001), .out(multiplexer_3_out));
  D_FF #(.Bits(3)) ans (.D(multiplexer_1_out), .C(clk), .Q(warnToOtherAns));  // open: nQ
  Multiplexer #(.Bits(2)) multiplexer_4 (.sel(car), .in_0(2'b01), .in_1(2'b10), .out(multiplexer_4_out));
  Multiplexer #(.Bits(3)) multiplexer_5 (
    .sel(jk_ff_2_q), .in_0(multiplexer_2_out), .in_1(multiplexer_3_out), .out(multiplexer_5_out));
  // Probe on warnToOtherAns
  Multiplexer #(.Bits(2)) multiplexer_6 (
    .sel(warning), .in_0(multiplexer_4_out), .in_1(2'b00), .out(multiplexer_6_out));
  Multiplexer #(.Bits(2)) multiplexer_7 (
    .sel(or_3_out), .in_0(state_q), .in_1(multiplexer_6_out), .out(multiplexer_7_out));
  or or_3 (or_3_out, car, human, warning);
  D_FF #(.Bits(2)) state (.D(multiplexer_7_out), .C(clk), .Q(state_q));  // open: nQ
  Comparator #(.Bits(2)) comparator_3 (.a(multiplexer_7_out), .b(state_q), .eq(comparator_3_eq));  // open: gt, lt
  Multiplexer #(.Bits(3)) multiplexer_8 (
    .sel(warncase), .in_0(multiplexer_5_out), .in_1({1'b0, warnAns[1], 1'b0}), .out(multiplexer_8_out));
  D_FF d_ff_1 (.D(d_ff_1_nq), .C(clk), .Q(warnAns[1]), .nQ(d_ff_1_nq));
  not not_1 (not_1_out, comparator_3_eq);
  Comparator #(.Bits(2)) comparator_4 (.a(state_q), .b(2'b01), .gt(carcase), .eq(humcase), .lt(warncase));
  and and_9 (statechange, or_3_out, not_1_out);
  Multiplexer #(.Bits(3)) multiplexer_9 (
    .sel(instantflip), .in_0(multiplexer_8_out), .in_1(warnToOtherAns), .out(multiplexer_9_out));
  LED led_1 (.in(multiplexer_9_out[0]));
  LED led_2 (.in(multiplexer_9_out[1]));
  LED led_3 (.in(multiplexer_9_out[2]));
  LED led_4 (.in(multiplexer_9_out[2]));
  LED led_5 (.in(multiplexer_9_out[1]));
  LED led_6 (.in(multiplexer_9_out[0]));

  // Other names for the same wires on the sheet: hum = human; warn = warning

  // Notes on the sheet:
  //   human
  //   car
endmodule
