// Digital circuit gcd.dig as structural Verilog
module gcd (
  input  start,
  input  [7:0] B,
  input  [7:0] A,
  input  clk,
  output [7:0] GCD
);

  wire and_1_out, busy, comparator_1_eq, d_ff_1_nq, Loading, not_1_out, start_t;
  wire [7:0] bold, d_ff_2_q, multiplexer_1_out, multiplexer_2_out, rem;

  Multiplexer #(.Bits(8)) multiplexer_1 (.sel(Loading), .in_0(bold), .in_1(A), .out(multiplexer_1_out));
  Multiplexer #(.Bits(8)) multiplexer_2 (.sel(Loading), .in_0(rem), .in_1(B), .out(multiplexer_2_out));
  D_FF d_ff_1 (.D(start), .C(clk), .nQ(d_ff_1_nq));  // open: Q
  D_FF #(.Bits(8)) d_ff_2 (.D(multiplexer_1_out), .C(clk), .Q(d_ff_2_q));  // open: nQ
  D_FF #(.Bits(8)) d_ff_3 (.D(multiplexer_2_out), .C(clk), .Q(bold));  // open: nQ
  and and_1 (and_1_out, start, d_ff_1_nq);
  not not_1 (not_1_out, busy);
  Div #(.Bits(8)) div_1 (.a(d_ff_2_q), .b(bold), .r(rem));  // open: q
  // Probe on bold
  and and_2 (Loading, start_t, not_1_out);
  D_FF d_ff_4 (.D(and_1_out), .C(clk), .Q(start_t));  // open: nQ
  Comparator #(.Bits(8)) comparator_1 (.a({8{1'b0}}), .b(rem), .eq(comparator_1_eq));  // open: gt, lt
  not not_2 (busy, comparator_1_eq);
  D_FF #(.Bits(8)) d_ff_5 (.D(bold), .C(comparator_1_eq), .Q(GCD));  // open: nQ

  // Other names for the same wires on the sheet: loadA[7:0] = A; loadB[7:0] = B

  // Notes on the sheet:
  //   B: default 9
  //   A: default 6
endmodule
