// Digital circuit s2017.dig as structural Verilog
module s2017 (
  input  [3:0] dividend,
  input  [3:0] divisor,
  output [3:0] quotient,
  output [3:0] remainder
);

  Div #(.Bits(4)) div_1 (.a(dividend), .b(divisor), .q(quotient), .r(remainder));
endmodule
