// Digital circuit s2021_1.dig as structural Verilog
module s2021_1 (
  input  [7:0] \input ,
  input  ADD,
  input  clk,
  input  reset,
  output [11:0] Z
);

  wire add_t, and_2_out, d_ff_1_nq, not_1_out;
  wire [7:0] multiplexer_1_out;
  wire [11:0] add_1_s, and_1_out, bitextender_1_out;

  not not_1 (not_1_out, reset);
  BitExtender #(.inputBits(1), .outputBits(12)) bitextender_1 (.in(not_1_out), .out(bitextender_1_out));
  assign and_1_out = bitextender_1_out & Z;  // And and_1, 12 bits wide
  D_FF d_ff_1 (.D(ADD), .C(clk), .nQ(d_ff_1_nq));  // open: Q
  Multiplexer #(.Bits(8)) multiplexer_1 (.sel(add_t), .in_0({8{1'b0}}), .in_1(\input ), .out(multiplexer_1_out));
  and and_2 (and_2_out, ADD, d_ff_1_nq);
  D_FF d_ff_2 (.D(and_2_out), .C(clk), .Q(add_t));  // open: nQ
  Add #(.Bits(12)) add_1 (.a(and_1_out), .b({4'b0000, multiplexer_1_out}), .c_i(1'b0), .s(add_1_s));  // open: c_o
  D_FF #(.Bits(12)) d_ff_3 (.D(add_1_s), .C(clk), .Q(Z));  // open: nQ

  // Other names for the same wires on the sheet: inp[7:0] = \input 
endmodule
