// Digital circuit s2021_2.dig as structural Verilog
module s2021_2 (
  input  btn,
  output [3:0] Z
);

  wire comparator_1_eq;
  wire [3:0] add_1_s, multiplexer_1_out;

  Comparator #(.Bits(4)) comparator_1 (.a(Z), .b(4'b1111), .eq(comparator_1_eq));  // open: gt, lt
  Multiplexer #(.Bits(4)) multiplexer_1 (
    .sel(comparator_1_eq), .in_0(4'b0011), .in_1(4'b0001), .out(multiplexer_1_out));
  Add #(.Bits(4)) add_1 (.a(Z), .b(multiplexer_1_out), .c_i(1'b0), .s(add_1_s));  // open: c_o
  D_FF #(.Bits(4)) d_ff_1 (.D(add_1_s), .C(btn), .Q(Z));  // open: nQ
endmodule
