// Digital circuit s2558_1.dig as structural Verilog
module s2558_1 (
  input  btn,
  output [3:0] Z
);

  wire comparator_1_eq;
  wire [3:0] add_1_s, d_ff_1_q, multiplexer_1_out;

  Comparator #(.Bits(4)) comparator_1 (.a(d_ff_1_q), .b(4'b1100), .eq(comparator_1_eq));  // open: gt, lt
  Multiplexer #(.Bits(4)) multiplexer_1 (
    .sel(comparator_1_eq), .in_0(4'b0011), .in_1(4'b0100), .out(multiplexer_1_out));
  Add #(.Bits(4)) add_1 (.a(d_ff_1_q), .b(multiplexer_1_out), .c_i(1'b0), .s(add_1_s));  // open: c_o
  D_FF #(.Bits(4)) d_ff_1 (.D(add_1_s), .C(btn), .Q(d_ff_1_q));  // open: nQ
  Add #(.Bits(4)) add_2 (.a(d_ff_1_q), .b(4'b0010), .c_i(1'b0), .s(Z));  // open: c_o
endmodule
