// Digital circuit 1.dig as structural Verilog
module _1 (
  input  [2:0] in_1,
  input  [2:0] in_2
);

  wire add_1_c_o;
  wire [3:0] add_2_s;

  Add #(.Bits(3)) add_1 (.a(in_1), .b(in_2), .c_i(1'b0), .c_o(add_1_c_o));  // open: s
  Add #(.Bits(4)) add_2 (.a(4'b0000), .b(4'b0000), .c_i(add_1_c_o), .s(add_2_s));  // open: c_o
  Seven_Seg_Hex seven_seg_hex_1 (.d(add_2_s), .dp(1'b0));
endmodule
